# Fritzing sketch Circuit-Diagram (saved by Fritzing 0.9.3b)
breadboards: 1

parts:
  Arduino_UNO = Arduino Uno (Rev3)
  HC-SR04_Ultrasonic_Sensor = hc-sr04
  L1 = Solenoid [part_number="Solenoid Valve"]
  Q1 = TRANSISTOR_NPN [part_number=BC547 package=to-92-ammo]
  R1 = RELAY-2 [part_number=Relay package=relay-g5v]
  Power_plug1 = Power plug [part_number="DC 12V"]
  R1_2 = Resistor [tolerance=±5% resistance=220 package=THT]
  D1 = Rectifier Diode [part_number=1N4001 package="300 mil [THT]"]
  Power_plug2 = Power plug [part_number="AC 230V"]
  J2 = female alternating pin header, 1 pin [form="♀ (female)" part_number="Extra PIN"]
  J1 = single row smd female pin header, 1 pin [form="♀ (female)" part_number="Extra PIN"]

nets:
  N1: Arduino_UNO.D9_PWM, HC-SR04_Ultrasonic_Sensor.Trig
  N2: Arduino_UNO.D10_PWM/SS, HC-SR04_Ultrasonic_Sensor.Echo
  N3: Arduino_UNO.D12/MISO, R1_2.Pin_0
  GND: Arduino_UNO.GND, HC-SR04_Ultrasonic_Sensor.GND, Q1.E, Power_plug1.GND
  N4: Arduino_UNO.D4, J1.pin1
  N5: Arduino_UNO.D6_PWM, J2.pin1
  5V: Arduino_UNO.5V, HC-SR04_Ultrasonic_Sensor.VCC
  N6: L1.pin1, Power_plug2.GND
  N7: L1.pin2, R1.10
  N8: Q1.B, R1_2.Pin_1
  N9: Q1.C, R1.9, D1.anode
  N10: R1.1, Power_plug2.VCC
  12V: R1.2, Power_plug1.VCC, D1.cathode

notes:
  Extra pins
